// Digital circuit cpu.dig as structural Verilog
module cpu (
  input  RESET,
  input  HALT,
  input  CONTINUE,
  input  CLKEN,
  input  STEP,
  input  clk
);

  wire _2x16bit_mux_1_p4, ADRSEL, CLK_t, CLK_t_t, Control_ishalted, Control_reset_2, CRYEN, FWEN, HALT_t,
       IOREN, IOWEN, nand_3_out, nand_4_out, nand_5_out, nand_6_out, nand_7_out, nand_8_out, nand_9_out,
       nand_10_out, nand_11_out, nand_12_out, OPSEL, PCSSEL, register_bank_1_p12, register_bank_1_p13,
       REGWEN, RESSEL, ZINV;
  wire [2:0] ALUOP, program_memory_1_rd, program_memory_1_ro1, program_memory_1_ro2;
  wire [3:0] program_counter_1_r, program_counter_1_r_2, program_counter_1_r_3, program_counter_1_r_4,
       register_bank_1_p7;
  wire [6:0] program_memory_1_opcode;
  wire [7:0] _2x8bit_mux_1_out, _8bit_alu_1_result, driver_1_out, program_memory_1_imm, register_bank_1_p6,
       register_bank_1_p10, register_bank_1_p11;
  wire [15:0] _2x16bit_mux_1_p1, _2x16bit_mux_1_p2, _2x16bit_mux_1_p3;
  wire [15:8] program_memory_1_imm_2;

  Seven_Seg_Hex seven_seg_hex_1 (.d(program_counter_1_r_4), .dp(1'b0));
  clock Control (
    .RESET(RESET), .HALT(HALT), .CONTINUE(CONTINUE), .CLKHALT(HALT_t), .CLKIN(clk), .STEP(STEP),
    .CLKEN(CLKEN), .ISHALTED(Control_ishalted), .RESET_2(Control_reset_2), .CLKOUT(CLK_t));
  Seven_Seg_Hex seven_seg_hex_2 (.d(program_counter_1_r_3), .dp(1'b0));
  Seven_Seg_Hex seven_seg_hex_3 (.d(program_counter_1_r_2), .dp(1'b0));
  Seven_Seg_Hex seven_seg_hex_4 (.d(program_counter_1_r), .dp(1'b0));
  LED HALTED (.in(Control_ishalted));
  nand nand_1 (CLK_t_t, CLK_t, CLK_t);
  program_counter program_counter_1 (
    .CLK(CLK_t_t), .W(_2x16bit_mux_1_p1), .CLR(Control_reset_2),
    .R({program_counter_1_r_4, program_counter_1_r_3, program_counter_1_r_2, program_counter_1_r}));
  // _2x16bit_mux _2x16bit_mux_1: pin names not known; wires that end beside it: _2x16bit_mux_1_p1, _2x16bit_mux_1_p2, _2x16bit_mux_1_p3, _2x16bit_mux_1_p4
  program_memory program_memory_1 (
    .ADR({program_counter_1_r_4, program_counter_1_r_3, program_counter_1_r_2, program_counter_1_r}),
    .OPCODE(program_memory_1_opcode), .RD(program_memory_1_rd), .RO1(program_memory_1_ro1),
    .RO2(program_memory_1_ro2), .IMM({program_memory_1_imm_2, program_memory_1_imm}));
  _16bit_incrementer _16bit_incrementer_1 (
    .IN({program_counter_1_r_4, program_counter_1_r_3, program_counter_1_r_2, program_counter_1_r}),
    .OUT(_2x16bit_mux_1_p2));
  oprom oprom_1 (
    .OPCODE(program_memory_1_opcode), .REGWEN(REGWEN), .IOREN(IOREN), .IOWEN(IOWEN), .PCSSEL(PCSSEL),
    .HALT(HALT_t), .OPSEL(OPSEL), .FWEN(FWEN), .ADRSEL(ADRSEL), .RESSEL(RESSEL), .ZINV(ZINV), .ALUOP(ALUOP),
    .CRYEN(CRYEN));
  nand nand_2 (_2x16bit_mux_1_p4, nand_3_out, nand_3_out);
  nand nand_3 (nand_3_out, PCSSEL, nand_4_out);
  nand nand_4 (nand_4_out, nand_6_out, nand_5_out);
  // register_bank register_bank_1: pin names not known; wires that end beside it: CLK_t, Control_reset_2, program_memory_1_rd, program_memory_1_ro1, program_memory_1_ro2, register_bank_1_p6, {4'b0000, register_bank_1_p7}, REGWEN, FWEN, register_bank_1_p10, register_bank_1_p11, register_bank_1_p12, register_bank_1_p13
  nand nand_5 (nand_5_out, nand_7_out, register_bank_1_p7[0]);
  nand nand_6 (nand_6_out, ZINV, nand_7_out);
  nand nand_7 (nand_7_out, ZINV, register_bank_1_p7[0]);
  _2x8bit_mux _2x8bit_mux_1 (.SEL(OPSEL), .B(program_memory_1_imm), .A(register_bank_1_p11), .OUT(_2x8bit_mux_1_out));
  // _2x16bit_mux _2x16bit_mux_2: pin names not known; wires that end beside it: ADRSEL, {program_memory_1_imm_2, program_memory_1_imm}, register_bank_1_p13, _2x16bit_mux_1_p3
  nand nand_8 (nand_8_out, register_bank_1_p12, CRYEN);
  nand nand_9 (nand_9_out, nand_8_out, nand_8_out);
  _8bit_alu _8bit_alu_1 (
    .OP(ALUOP), .A(register_bank_1_p10), .B(_2x8bit_mux_1_out), .CIN(nand_9_out),
    .RESULT(_8bit_alu_1_result), .ZERO(register_bank_1_p7[0]), .NEGATIVE(register_bank_1_p7[1]),
    .CARRY(register_bank_1_p7[2]), .OVERFLOW(register_bank_1_p7[3]));
  _2x8bit_mux _2x8bit_mux_2 (.SEL(RESSEL), .B(driver_1_out), .A(_8bit_alu_1_result), .OUT(register_bank_1_p6));
  nand nand_10 (nand_10_out, IOWEN, CLK_t);
  nand nand_11 (nand_11_out, nand_10_out, nand_10_out);
  assign driver_1_out = nand_12_out ? register_bank_1_p11 : 8'bz;  // Driver driver_1
  RAMSinglePortSel #(.AddrBits(16), .Bits(8)) ramsingleportsel_1 (
    .A(_2x16bit_mux_1_p3), .CS(1'b1), .WE(nand_11_out), .OE(IOREN), .D(driver_1_out));
  nand nand_12 (nand_12_out, IOREN, IOREN);

  // Notes on the sheet:
  //   clk: Hz: 100
endmodule
